// Logisim project 16-bit.circ as structural Verilog: 2 circuits, main circuit main
module main (
  input  cin,
  input  M,
  input  B,
  input  A,
  output S0,
  output Cout
);

  wire xor_1_out;

  xor xor_1 (xor_1_out, M, B);
  Adder #(.width(1)) adder_1 (.a(xor_1_out), .b(A), .out(S0), .cin(cin), .cout(Cout));
endmodule

module full_adder (
  input  in_1,
  input  [15:0] A,
  input  [15:0] B,
  output V,
  output C,
  output [15:0] out_6
);

  wire _0_cout, _1_cout, _2_cout, _3_cout, _4_cout, _5_cout, _6_cout, _7_cout, _8_cout, _9_cout, _10_cout,
       _11_cout, _12_cout, _13_cout, _14_cout;

  main _0 (.M(in_1), .B(A[0]), .A(B[0]), .Cout(_0_cout), .S0(out_6[0]), .cin(in_1));
  main _1 (.M(in_1), .B(B[1]), .A(A[1]), .Cout(_1_cout), .S0(out_6[1]), .cin(_0_cout));
  main _2 (.M(in_1), .B(B[2]), .A(A[2]), .Cout(_2_cout), .S0(out_6[2]), .cin(_1_cout));
  main _3 (.M(in_1), .B(B[3]), .A(A[3]), .Cout(_3_cout), .S0(out_6[3]), .cin(_2_cout));
  main _4 (.M(in_1), .B(B[4]), .A(A[4]), .Cout(_4_cout), .S0(out_6[4]), .cin(_3_cout));
  main _5 (.M(in_1), .B(B[5]), .A(A[5]), .Cout(_5_cout), .S0(out_6[5]), .cin(_4_cout));
  main _6 (.M(in_1), .B(B[6]), .A(A[6]), .Cout(_6_cout), .S0(out_6[6]), .cin(_5_cout));
  main _7 (.M(in_1), .B(B[7]), .A(A[7]), .Cout(_7_cout), .S0(out_6[7]), .cin(_6_cout));
  main _8 (.M(in_1), .B(B[8]), .A(A[8]), .Cout(_8_cout), .S0(out_6[8]), .cin(_7_cout));
  main _9 (.M(in_1), .B(B[9]), .A(A[9]), .Cout(_9_cout), .S0(out_6[9]), .cin(_8_cout));
  main _10 (.M(in_1), .B(B[10]), .A(A[10]), .Cout(_10_cout), .S0(out_6[10]), .cin(_9_cout));
  main _11 (.M(in_1), .B(B[11]), .A(A[11]), .Cout(_11_cout), .S0(out_6[11]), .cin(_10_cout));
  main _12 (.M(in_1), .B(B[12]), .A(A[12]), .Cout(_12_cout), .S0(out_6[12]), .cin(_11_cout));
  main _13 (.M(in_1), .B(B[13]), .A(A[13]), .Cout(_13_cout), .S0(out_6[13]), .cin(_12_cout));
  main _14 (.M(in_1), .B(B[14]), .A(A[14]), .Cout(_14_cout), .S0(out_6[14]), .cin(_13_cout));
  main _15 (.M(in_1), .B(B[15]), .A(A[15]), .Cout(C), .S0(out_6[15]), .cin(_14_cout));
  xor xor_1 (V, _14_cout, C);
endmodule
