// Logisim project 16.circ as structural Verilog: 1 circuit, main circuit main
module main (
  input  in_1,
  input  in_2,
  input  in_3,
  input  in_4,
  input  in_5
);

  wire adder_1_out, adder_2_cout, adder_2_out, and_1_out, clock_1_out, d_ff_1_q, shift_register_1_out,
       shift_register_2_out, xor_1_out;

  Clock clock_1 (.out(clock_1_out));
  Shift_Register #(.length(16)) shift_register_1 (
    .shift(in_2), .in(adder_2_out), .clk(clock_1_out), .out(shift_register_1_out));  // open: load, clr, d0, q0, d1, q1, d2, q2, d3, q3, d4, q4, d5, q5, d6, q6, d7, q7, d8, q8, d9, q9, d10, q10, d11, q11, d12, q12, d13, q13, d14, q14, d15, q15
  Shift_Register #(.length(16)) shift_register_2 (
    .shift(in_2), .in(in_3), .clk(clock_1_out), .out(shift_register_2_out));  // open: load, clr, d0, q0, d1, q1, d2, q2, d3, q3, d4, q4, d5, q5, d6, q6, d7, q7, d8, q8, d9, q9, d10, q10, d11, q11, d12, q12, d13, q13, d14, q14, d15, q15
  and and_1 (and_1_out, in_2, clock_1_out);
  xor xor_1 (xor_1_out, shift_register_2_out, in_5);
  Adder #(.width(1)) adder_1 (.a(xor_1_out), .b(in_5), .out(adder_1_out), .cin(in_1));  // open: cout
  Adder #(.width(1)) adder_2 (
    .a(shift_register_1_out), .b(adder_1_out), .out(adder_2_out), .cin(d_ff_1_q), .cout(adder_2_cout));
  D_Flip_Flop d_ff_1 (.clk(and_1_out), .D(adder_2_cout), .Q(d_ff_1_q), .reset(in_4));  // open: Qn, preset, en
endmodule
